// Logisim project MATERIAL EXTRA - ALARME - PROJ. DE ENSINO.circ as structural Verilog: 1 circuit, main circuit main
module main (
  input  Sens__Mov,
  input  \Cent__Incêndio ,
  input  \Cent__Vibração ,
  output Alarme
);

  or or_1 (Alarme, Sens__Mov, \Cent__Incêndio , \Cent__Vibração );
endmodule
