// Logisim project MATERIAL EXTRA - XOR - PROJ. DE ENSINO - LABORATÓRIO DE.circ as structural Verilog: 1 circuit, main circuit main
module main (
  input  E1,
  input  E2,
  output S
);

  wire and_1_out, and_2_out, not_1_out, not_2_out;

  not not_1 (not_1_out, E1);
  and and_1 (and_1_out, not_1_out, E2);
  and and_2 (and_2_out, E1, not_2_out);
  not not_2 (not_2_out, E2);
  or or_1 (S, and_1_out, and_2_out);
endmodule
